// Logisim project Q10_4 bit gray Counrter.circ as structural Verilog: 1 circuit, main circuit main
module main (
  output Q0,
  output Q1,
  output Q2,
  output Q3
);

  wire and_1_out, and_2_out, and_3_out, and_4_out, and_5_out, and_6_out, and_7_out, and_8_out, and_9_out,
       Clock_out, j_k_ff_1_qn, j_k_ff_2_qn, j_k_ff_3_qn, j_k_ff_4_qn, or_1_out, or_2_out, or_3_out,
       xor_1_out, xor_2_out, xor_3_out;

  ExactlyOne xor_1 (.out(xor_1_out), .in0(Q1), .in1(Q2), .in2(Q3));
  or or_1 (or_1_out, xor_1_out, and_1_out);
  ExactlyOne xor_2 (.out(xor_2_out), .in0(j_k_ff_3_qn), .in1(j_k_ff_2_qn), .in2(j_k_ff_1_qn));
  and and_1 (and_1_out, Q1, Q2, Q3);
  or or_2 (or_2_out, xor_2_out, and_2_out);
  and and_2 (and_2_out, j_k_ff_3_qn, j_k_ff_2_qn, j_k_ff_1_qn);
  and and_3 (and_3_out, j_k_ff_4_qn, j_k_ff_3_qn, j_k_ff_2_qn);
  and and_4 (and_4_out, j_k_ff_4_qn, Q1, j_k_ff_1_qn);
  xor xor_3 (xor_3_out, Q2, Q3);
  and and_5 (and_5_out, xor_3_out, Q0);
  and and_6 (and_6_out, j_k_ff_4_qn, Q1, Q3);
  and and_7 (and_7_out, j_k_ff_4_qn, j_k_ff_3_qn, Q2);
  and and_8 (and_8_out, Q0, j_k_ff_2_qn, j_k_ff_1_qn);
  and and_9 (and_9_out, Q0, Q2, Q3);
  or or_3 (or_3_out, and_8_out, and_9_out);
  Clock Clock (.out(Clock_out));
  J_K_Flip_Flop j_k_ff_1 (
    .J(and_7_out), .clk(Clock_out), .K(and_3_out), .Q(Q3), .Qn(j_k_ff_1_qn));  // open: preset, en, reset
  J_K_Flip_Flop j_k_ff_2 (
    .J(and_4_out), .clk(Clock_out), .K(and_6_out), .Q(Q2), .Qn(j_k_ff_2_qn));  // open: preset, en, reset
  J_K_Flip_Flop j_k_ff_3 (
    .J(or_3_out), .clk(Clock_out), .K(and_5_out), .Q(Q1), .Qn(j_k_ff_3_qn));  // open: preset, en, reset
  J_K_Flip_Flop j_k_ff_4 (
    .J(or_2_out), .clk(Clock_out), .K(or_1_out), .Q(Q0), .Qn(j_k_ff_4_qn));  // open: preset, en, reset

  // Notes on the sheet:
  //   K0
  //    J0
  //    K3
  //   K1
  //   J2
  //   K2
  //   J3
  //   J1
endmodule
