// Logisim project Q11_1 3 5 7 Counter.circ as structural Verilog: 1 circuit, main circuit main
module main (
  input  Enable,
  output Q0,
  output Q1,
  output Q2
);

  wire and_1_out, clock_1_out, j_k_ff_1_qn, j_k_ff_2_qn;

  and and_1 (and_1_out, Enable, Q1);
  Clock clock_1 (.out(clock_1_out));
  J_K_Flip_Flop j_k_ff_1 (
    .J(and_1_out), .clk(clock_1_out), .K(and_1_out), .Q(Q2), .Qn(j_k_ff_1_qn));  // open: preset, en, reset
  J_K_Flip_Flop j_k_ff_2 (
    .J(Enable), .clk(clock_1_out), .K(Enable), .Q(Q1), .Qn(j_k_ff_2_qn));  // open: preset, en, reset

  assign Q0 = Enable;

  // Notes on the sheet:
  //   J1 K1
  //   J1 K1
  //   1 3 5 7 Counter
endmodule
