// Logisim project Q12_Sequence Generator 1101101.circ as structural Verilog: 1 circuit, main circuit main
module main (
  input  Enable,
  output Q0_Sequence_1101101,
  output Q1,
  output Q2,
  output Q3
);

  wire and_1_out, and_2_out, and_3_out, Clock_out, j_k_ff_1_qn, j_k_ff_2_qn, j_k_ff_3_qn, j_k_ff_4_qn;

  and and_1 (and_1_out, Q0_Sequence_1101101, j_k_ff_4_qn);
  and and_2 (and_2_out, j_k_ff_1_qn, j_k_ff_2_qn);
  and and_3 (and_3_out, Q1, j_k_ff_1_qn);
  Clock Clock (.out(Clock_out));
  J_K_Flip_Flop j_k_ff_1 (
    .J(Enable), .clk(Clock_out), .K(Q1), .Q(Q0_Sequence_1101101), .Qn(j_k_ff_1_qn));  // open: preset, en, reset
  J_K_Flip_Flop j_k_ff_2 (
    .J(and_1_out), .clk(Clock_out), .K(j_k_ff_3_qn), .Q(Q1), .Qn(j_k_ff_2_qn));  // open: preset, en, reset
  J_K_Flip_Flop j_k_ff_3 (.J(and_2_out), .clk(Clock_out), .K(Q1), .Q(Q2), .Qn(j_k_ff_3_qn));  // open: preset, en, reset
  J_K_Flip_Flop j_k_ff_4 (
    .J(and_3_out), .clk(Clock_out), .K(Enable), .Q(Q3), .Qn(j_k_ff_4_qn));  // open: preset, en, reset

  // Notes on the sheet:
  //   J0
  //   J1
  //   K0
  //   K1
  //   J2
  //   K2
  //   J3
  //   K3
endmodule
