// Logisim project Q13_Up Down Counetr.circ as structural Verilog: 1 circuit, main circuit main
module main (
  input  B0,
  input  B1,
  input  B2,
  output a,
  output b,
  output c,
  output d,
  output e,
  output f,
  output g
);

  wire A_prime_B_out, A_prime_B_prime_out, A_prime_C_out, A_prime_C_prime_out, AB_out, AB_prime_C_out,
       AC_out, B_prime_C_out, BC_prime_out, not_1_out, not_2_out, not_3_out;

  not not_1 (not_1_out, B0);
  not not_2 (not_2_out, B1);
  not not_3 (not_3_out, B2);
  and A_prime_C_prime (A_prime_C_prime_out, not_1_out, not_3_out);
  and AC (AC_out, B0, B2);
  or or_1 (a, A_prime_C_prime_out, AC_out, B1);
  or or_2 (b, A_prime_B_prime_out, AB_out, not_3_out);
  and A_prime_B_prime (A_prime_B_prime_out, not_1_out, not_2_out);
  and AB (AB_out, B0, B1);
  or or_3 (c, B2, not_2_out, B0);
  and AB_prime_C (AB_prime_C_out, B0, not_2_out, B2);
  or or_4 (d, AB_prime_C_out, A_prime_B_out, BC_prime_out, A_prime_C_prime_out);
  and A_prime_B (A_prime_B_out, not_1_out, B1);
  and BC_prime (BC_prime_out, B1, not_3_out);
  or or_5 (e, A_prime_C_prime_out, A_prime_B_out);
  and A_prime_C (A_prime_C_out, not_1_out, B2);
  or or_6 (f, A_prime_B_prime_out, A_prime_C_out, B_prime_C_out);
  and B_prime_C (B_prime_C_out, not_2_out, B2);
  or or_7 (g, BC_prime_out, B_prime_C_out, BC_prime_out);

  // Notes on the sheet:
  //   A
  //   B
  //   C
  //   Up Down Counter
endmodule
