// Logisim project Q1_T Flip-Flop.circ as structural Verilog: 1 circuit, main circuit main
module main (
  input  T,
  output out_2,
  output out_3
);

  wire and_1_out, and_2_out, clock_1_out;

  Clock clock_1 (.out(clock_1_out));
  and and_1 (and_1_out, out_2, T, clock_1_out);
  and and_2 (and_2_out, clock_1_out, T, out_3);
  not nor_1 (out_2, and_1_out);  // NOR_Gate
  nor nor_2 (out_3, out_2, and_2_out);

  // Notes on the sheet:
  //   T Flip-Flop Using Gates
endmodule
