// Logisim project Q3_Full Adder Using Demux.circ as structural Verilog: 1 circuit, main circuit main
module main (
  input  Input,
  input  Enable,
  input  [2:0] Select_Lines,
  output Sum,
  output Carry
);

  wire demultiplexer_1_out0, demultiplexer_1_out1, demultiplexer_1_out2, demultiplexer_1_out3,
       demultiplexer_1_out4, demultiplexer_1_out5, demultiplexer_1_out6, demultiplexer_1_out7;

  Demultiplexer #(.select(3)) demultiplexer_1 (
    .out0(demultiplexer_1_out0), .out1(demultiplexer_1_out1), .out2(demultiplexer_1_out2),
    .out3(demultiplexer_1_out3), .out4(demultiplexer_1_out4), .out5(demultiplexer_1_out5),
    .out6(demultiplexer_1_out6), .out7(demultiplexer_1_out7), .in(Input), .sel(Select_Lines), .en(Enable));
  or or_1 (Sum, demultiplexer_1_out1, demultiplexer_1_out2, demultiplexer_1_out4, demultiplexer_1_out7);
  or or_2 (Carry, demultiplexer_1_out3, demultiplexer_1_out5, demultiplexer_1_out6, demultiplexer_1_out7);

  // Notes on the sheet:
  //   FULL ADDER USING 1:8 DEMUX
  //   Y0
  //   Y1
  //   Y2
  //   Y3
  //   Y4
  //   Y5
  //   Y6
  //   Y7
endmodule
