// Logisim project Q4_Eight bit Magnitude Comparator using 4 bit Magnitude Comparator.circ as structural Verilog: 1 circuit, main circuit main
module main (
  input  [3:0] in_1,
  input  [3:0] in_2,
  input  [3:0] in_3,
  input  [3:0] in_4
);

  wire comparator_1_eq, comparator_1_gt, comparator_1_lt, comparator_2_eq, comparator_2_gt, comparator_2_lt,
       comparator_3_gt, comparator_3_lt, comparator_4_eq, comparator_5_gt, comparator_5_lt;

  Comparator #(.width(4), .mode("unsigned")) comparator_1 (
    .a(in_1), .b(in_2), .gt(comparator_1_gt), .eq(comparator_1_eq), .lt(comparator_1_lt));
  Comparator #(.width(4), .mode("unsigned")) comparator_2 (
    .a(in_3), .b(in_4), .gt(comparator_2_gt), .eq(comparator_2_eq), .lt(comparator_2_lt));
  Comparator #(.width(1), .mode("unsigned")) comparator_3 (
    .a(comparator_1_gt), .b(comparator_2_gt), .gt(comparator_3_gt), .lt(comparator_3_lt));  // open: eq
  Comparator #(.width(1), .mode("unsigned")) comparator_4 (
    .a(comparator_1_eq), .b(comparator_2_eq), .eq(comparator_4_eq));  // open: gt, lt
  Comparator #(.width(1), .mode("unsigned")) comparator_5 (
    .a(comparator_1_lt), .b(comparator_2_lt), .gt(comparator_5_gt), .lt(comparator_5_lt));  // open: eq

  // Notes on the sheet:
  //   8 bit comparator using 4 bit comparator
endmodule
