// Logisim project Q5_Parity Checker.circ as structural Verilog: 1 circuit, main circuit main
module main (
  input  P,
  input  A,
  input  B,
  input  C,
  output Even_Parity_Error
);

  wire xor_1_out, xor_2_out;

  xor xor_1 (xor_1_out, P, A);
  xor xor_2 (xor_2_out, B, C);
  xor xor_3 (Even_Parity_Error, xor_1_out, xor_2_out);

  // Notes on the sheet:
  //   Parity Checker
endmodule
