// Logisim project Q5_Togather Parity Generator and Checker.circ as structural Verilog: 1 circuit, main circuit main
module main (
  input  A,
  input  B,
  input  C,
  input  in_4,
  output Odd_Parity,
  output Even_Parity,
  output Even_Parity_Error
);

  wire xor_1_out, xor_3_out, xor_4_out;

  xor xor_1 (xor_1_out, A, B);
  xor xor_2 (Even_Parity, xor_1_out, C);
  not not_1 (Odd_Parity, Even_Parity);
  xor xor_3 (xor_3_out, in_4, C);
  xor xor_4 (xor_4_out, B, A);
  xor xor_5 (Even_Parity_Error, xor_3_out, xor_4_out);

  // Notes on the sheet:
  //   Parity Generator and Checker Togather
endmodule
