// Logisim project Q6_8 to3  Priority Encoder.circ as structural Verilog: 1 circuit, main circuit main
module main (
  input  D0,
  input  D1,
  input  D2,
  input  D3,
  input  D4,
  input  D5,
  input  D6,
  input  D7,
  output Y2,
  output Y1,
  output Y0,
  output V
);

  wire and_1_out, and_2_out, and_3_out, and_4_out, and_5_out, not_1_out, not_2_out, not_3_out, not_4_out,
       not_5_out, not_6_out, not_7_out, not_8_out;

  not not_1 (not_1_out, D0);
  not not_2 (not_2_out, D1);
  not not_3 (not_3_out, D2);
  not not_4 (not_4_out, D3);
  not not_5 (not_5_out, D4);
  not not_6 (not_6_out, D5);
  not not_7 (not_7_out, D6);
  not not_8 (not_8_out, D7);
  or or_1 (Y2, D4, D5, D6, D7);
  and and_1 (and_1_out, D3, not_5_out, not_6_out);
  and and_2 (and_2_out, D2, not_5_out, not_6_out);
  or or_2 (Y1, D6, and_1_out, and_2_out, D7);
  and and_3 (and_3_out, D3, not_5_out, not_6_out, not_7_out, not_8_out);
  and and_4 (and_4_out, D1, not_3_out, not_4_out, not_5_out, not_6_out, not_7_out, not_8_out);
  or or_3 (Y0, and_4_out, and_3_out, and_5_out, D7);
  and and_5 (and_5_out, D5, not_7_out, not_8_out);
  or or_4 (V, D0, D1, D2, D3, D4, D5, D6, D7);

  // Notes on the sheet:
  //   8 to3  Priority Encoder
endmodule
