// Logisim project Q8_4 bit Asynchronus Up Counter.circ as structural Verilog: 1 circuit, main circuit main
module main (
  input  Preset,
  input  Enable,
  input  Clear,
  output A0,
  output A2,
  output A3,
  output A4
);

  wire Clk_out, d_ff_1_qn, d_ff_2_qn, d_ff_3_qn, d_ff_4_qn;

  Clock Clk (.out(Clk_out));
  D_Flip_Flop d_ff_1 (
    .clk(Clk_out), .D(d_ff_1_qn), .Q(A0), .Qn(d_ff_1_qn), .preset(Preset), .en(Enable), .reset(Clear));
  D_Flip_Flop d_ff_2 (
    .clk(d_ff_1_qn), .D(d_ff_2_qn), .Q(A2), .Qn(d_ff_2_qn), .preset(Preset), .en(Enable), .reset(Clear));
  D_Flip_Flop d_ff_3 (
    .clk(d_ff_2_qn), .D(d_ff_3_qn), .Q(A3), .Qn(d_ff_3_qn), .preset(Preset), .en(Enable), .reset(Clear));
  D_Flip_Flop d_ff_4 (
    .clk(d_ff_3_qn), .D(d_ff_4_qn), .Q(A4), .Qn(d_ff_4_qn), .preset(Preset), .en(Enable), .reset(Clear));

  // Notes on the sheet:
  //   4 bit Asynchronus up counter using D Flip-Flop
endmodule
