// Logisim project Q9_4 bit Synchronus Down Counter.circ as structural Verilog: 1 circuit, main circuit main
module main (
  input  in_1,
  output Q0,
  output Q1,
  output Q2,
  output Q3
);

  wire and_1_out, and_2_out, clk_out, j_k_ff_1_qn, j_k_ff_2_qn, j_k_ff_3_qn;

  Clock clk (.out(clk_out));
  J_K_Flip_Flop j_k_ff_1 (.J(in_1), .clk(clk_out), .K(in_1), .Q(Q0), .Qn(j_k_ff_1_qn));  // open: preset, en, reset
  J_K_Flip_Flop j_k_ff_2 (
    .J(j_k_ff_1_qn), .clk(clk_out), .K(j_k_ff_1_qn), .Q(Q1), .Qn(j_k_ff_2_qn));  // open: preset, en, reset
  and and_1 (and_1_out, j_k_ff_1_qn, j_k_ff_2_qn);
  J_K_Flip_Flop j_k_ff_3 (
    .J(and_1_out), .clk(clk_out), .K(and_1_out), .Q(Q2), .Qn(j_k_ff_3_qn));  // open: preset, en, reset
  and and_2 (and_2_out, and_1_out, j_k_ff_3_qn);
  J_K_Flip_Flop j_k_ff_4 (.J(and_2_out), .clk(clk_out), .K(and_2_out), .Q(Q3));  // open: Qn, preset, en, reset

  // Notes on the sheet:
  //   4 bit Synchronus down counter using JK Flip-Flop
endmodule
