// Logisim project Q9_4 bit Synchronus Up Counter.circ as structural Verilog: 1 circuit, main circuit main
module main (
  input  in_1,
  output Q0,
  output Q1,
  output Q2,
  output Q3
);

  wire and_1_out, and_2_out, Clk_out;

  Clock Clk (.out(Clk_out));
  J_K_Flip_Flop j_k_ff_1 (.J(in_1), .clk(Clk_out), .K(in_1), .Q(Q0));  // open: Qn, preset, en, reset
  J_K_Flip_Flop j_k_ff_2 (.J(Q0), .clk(Clk_out), .K(Q0), .Q(Q1));  // open: Qn, preset, en, reset
  and and_1 (and_1_out, Q1, Q0);
  J_K_Flip_Flop j_k_ff_3 (.J(and_1_out), .clk(Clk_out), .K(and_1_out), .Q(Q2));  // open: Qn, preset, en, reset
  and and_2 (and_2_out, and_1_out, Q2);
  J_K_Flip_Flop j_k_ff_4 (.J(and_2_out), .clk(Clk_out), .K(and_2_out), .Q(Q3));  // open: Qn, preset, en, reset

  // Notes on the sheet:
  //   4 bit Synchronus up counter using JK Flip-Flop
endmodule
