// Logisim project Full Adder Cricuit.circ as structural Verilog: 1 circuit, main circuit main
module main (
  input  A,
  input  B,
  input  Cin,
  output out_4,
  output out_5
);

  wire and_1_out, and_2_out, xor_1_out;

  xor xor_1 (xor_1_out, A, B);
  and and_1 (and_1_out, Cin, xor_1_out);
  and and_2 (and_2_out, A, B);
  xor xor_2 (out_4, xor_1_out, Cin);
  or or_1 (out_5, and_1_out, and_2_out);

  // Notes on the sheet:
  //   FULL ADDER CIRCUIT
  //   S = AB' + B'C + C'A
  //   C =( AB' + BC )' Cin+ AB
endmodule
