// Logisim project Half Adder circuit.circ as structural Verilog: 1 circuit, main circuit main
module main (
  input  in_1,
  input  in_2,
  output S___AB_prime___A_prime_B,
  output C___AB
);

  xor xor_1 (S___AB_prime___A_prime_B, in_1, in_2);
  and and_1 (C___AB, in_1, in_2);

  // Notes on the sheet:
  //   HALF ADDER
endmodule
