// Logisim project Mux using NAND gate.circ as structural Verilog: 1 circuit, main circuit main
module main (
  input  S2,
  input  S1,
  input  I0,
  input  I1,
  input  I2,
  input  I3,
  output Y
);

  wire _7400_2_out, _7400_3_out, _7400_out, _7410_2_out, _7410_3_out, _7410_4_out, _7410_5_out, _7410_out;

  nand _7400 (_7400_out, S1, S1);
  nand _7400_2 (_7400_2_out, S2, S2);
  nand _7410 (_7410_out, I0, _7400_out, _7400_2_out);
  nand _7410_2 (_7410_2_out, I1, _7400_out, S2);
  nand _7410_3 (_7410_3_out, I2, S1, _7400_2_out);
  nand _7410_4 (_7410_4_out, I3, S1, S2);
  nand _7410_5 (_7410_5_out, _7410_out, _7410_2_out, _7410_3_out);
  nand _7400_3 (_7400_3_out, _7410_5_out, _7410_5_out);
  nand _7400_4 (Y, _7400_3_out, _7410_4_out);
endmodule
