// Logisim project binary to decimal converter.circ as structural Verilog: 1 circuit, main circuit main
module main (
  input  [3:0] in_1,
  output _0,
  output _1,
  output _2,
  output _3,
  output _4,
  output _5,
  output _6,
  output _7,
  output _8,
  output _9
);

  Decoder #(.select(4), .enable("false")) decoder_1 (
    .out0(_0), .out1(_1), .out2(_2), .out3(_3), .out4(_4), .out5(_5), .out6(_6), .out7(_7), .out8(_8),
    .out9(_9), .sel(in_1));  // open: out10, out11, out12, out13, out14, out15

  // Notes on the sheet:
  //   Binary to decimal decoder
endmodule
