// Logisim project decoder(2 bits).circ as structural Verilog: 1 circuit, main circuit main
module main (
  input  [1:0] in_1,
  output _1,
  output out_3,
  output _2,
  output _3
);

  Decoder #(.select(2), .enable("false")) decoder_1 (.out0(_1), .out1(out_3), .out2(_2), .out3(_3), .sel(in_1));

  // Notes on the sheet:
  //   Decoder
  //   0
endmodule
