// Logisim project eight_three_using gates.circ as structural Verilog: 1 circuit, main circuit main
module main (
  input  in_1,
  input  in_2,
  input  in_3,
  input  in_4,
  input  in_5,
  input  in_6,
  input  in_7,
  input  in_8,
  input  in_9
);

  wire not_3_out, not_4_out, not_5_out;

  // NOT_Gate not_1 has open pins: in=in_2, out=open
  // NOT_Gate not_2 has open pins: in=in_3, out=open
  not not_3 (not_3_out, in_4);
  not not_4 (not_4_out, in_5);
  not not_5 (not_5_out, in_6);
  // NOT_Gate not_6 has open pins: in=in_7, out=open
  // NOT_Gate not_7 has open pins: in=in_8, out=open
  // NOT_Gate not_8 has open pins: in=in_9, out=open
  // AND_Gate and_1 has open pins: in0=in_3, in1=not_3_out, in2=not_4_out, in3=not_5_out, out=open
  // OR_Gate or_1 has open pins: in0=in_4, in1=in_5, out=open
  or or_2 (in_1, in_2, in_3, in_4, in_5, in_6, in_7, in_8, in_9);
endmodule
