// Logisim project four_one MUX.circ as structural Verilog: 1 circuit, main circuit main
module main (
  input  I0,
  input  I1,
  input  I2,
  input  in_4,
  input  S0,
  input  ENABLE,
  input  S1,
  output OUTPUT
);

  wire multiplexer_1_out, multiplexer_2_out;

  Multiplexer multiplexer_1 (.in0(I0), .in1(I1), .out(multiplexer_1_out), .sel(S0), .en(ENABLE));
  Multiplexer multiplexer_2 (.in0(I2), .in1(in_4), .out(multiplexer_2_out), .sel(S0), .en(ENABLE));
  Multiplexer multiplexer_3 (.in0(multiplexer_1_out), .in1(multiplexer_2_out), .out(OUTPUT), .sel(S1), .en(ENABLE));

  // Notes on the sheet:
  //   I3
  //   4:1 USING 2:1 MUX
endmodule
