// Logisim project four_to_two priority enocder.circ as structural Verilog: 1 circuit, main circuit main
module main (
  input  i0,
  input  i1,
  input  i2,
  input  i3,
  input  in_5,
  output out_6,
  output [1:0] out_7,
  output out_8
);

  Priority_Encoder #(.select(2)) priority_encoder_1 (
    .in0(i0), .in1(i1), .in2(i2), .in3(i3), .out(out_7), .gs(out_8), .en_out(out_6), .en_in(in_5));

  // Notes on the sheet:
  //   4:2 Priority Encoder
endmodule
