// Logisim project two_one MUX.circ as structural Verilog: 1 circuit, main circuit main
module main (
  input  in_1,
  input  in_2,
  input  in_3,
  input  in_4,
  output out_5
);

  Multiplexer multiplexer_1 (.in0(in_1), .in1(in_2), .out(out_5), .sel(in_3), .en(in_4));

  // Notes on the sheet:
  //   2 : 1 MUX
endmodule
