// Logisim project two_one demux.circ as structural Verilog: 1 circuit, main circuit main
module main (
  input  in_1,
  input  in_2,
  input  in_3,
  output \output ,
  output out_5
);

  Demultiplexer demultiplexer_1 (.out0(\output ), .out1(out_5), .in(in_1), .sel(in_3), .en(in_2));

  // Notes on the sheet:
  //   input
  //   2:1 Demux
  //   S1
  //   S0
endmodule
