// Logisim project Assignment 4.circ as structural Verilog: 2 circuits, main circuit main
module main (
  input  [3:0] B,
  input  [3:0] in_2,
  input  Carry_in,
  input  Command,
  input  S,
  output [3:0] C,
  output out_7
);

  wire [3:0] adder_1_out, and_1_out;

  Adder #(.width(4)) adder_1 (.a(B), .b(in_2), .out(adder_1_out), .cin(Carry_in), .cout(out_7));
  Multiplexer #(.width(4)) multiplexer_1 (.in0(adder_1_out), .in1(and_1_out), .out(C), .sel(Command), .en(S));
  assign and_1_out = in_2 & B;  // AND_Gate and_1, 4 bits wide

  // Notes on the sheet:
  //   A
  //   4 bit FULL adder
  //   Carry out
  //   4 bit AND operator
endmodule

module data_path (
  input  in_1,
  input  [3:0] _1,
  input  [3:0] _2,
  input  in_4,
  input  in_5,
  input  [1:0] S2,
  input  in_7,
  input  S1,
  input  Cmd_0,
  input  in_10,
  input  Cmd_1,
  input  CY_in,
  input  in_13,
  input  in_14,
  input  in_15,
  input  in_16,
  input  in_17,
  input  in_18,
  output CY_out
);

  wire clock_1_out;
  wire [3:0] ALU_c, controlled_buffer_1_out, controlled_buffer_2_out, controlled_buffer_3_out,
       controlled_buffer_4_out, controlled_buffer_7_out, controlled_buffer_9_out, controlled_buffer_10_out,
       multiplexer_1_out, register_1_q, register_2_q, register_3_q, register_4_q, register_5_q;

  Clock clock_1 (.out(clock_1_out));
  assign controlled_buffer_1_out = in_4 ? controlled_buffer_4_out : 4'bz;  // Controlled_Buffer controlled_buffer_1
  Register #(.width(4)) register_1 (.D(controlled_buffer_1_out), .Q(register_1_q), .clk(clock_1_out));  // open: en, clr
  assign controlled_buffer_2_out = in_10 ? controlled_buffer_4_out : 4'bz;  // Controlled_Buffer controlled_buffer_2
  Register #(.width(4)) register_2 (.D(controlled_buffer_2_out), .Q(register_2_q), .clk(clock_1_out));  // open: en, clr
  assign controlled_buffer_3_out = in_15 ? controlled_buffer_4_out : 4'bz;  // Controlled_Buffer controlled_buffer_3
  Register #(.width(4)) register_3 (.D(controlled_buffer_3_out), .Q(register_3_q), .clk(clock_1_out));  // open: en, clr
  assign controlled_buffer_4_out = in_7 ? register_1_q : 4'bz;  // Controlled_Buffer controlled_buffer_4
  assign controlled_buffer_4_out = in_13 ? register_2_q : 4'bz;  // Controlled_Buffer controlled_buffer_5
  assign controlled_buffer_4_out = in_17 ? register_3_q : 4'bz;  // Controlled_Buffer controlled_buffer_6
  assign controlled_buffer_7_out = in_1 ? controlled_buffer_4_out : 4'bz;  // Controlled_Buffer controlled_buffer_7
  assign controlled_buffer_4_out = in_18 ? register_5_q : 4'bz;  // Controlled_Buffer controlled_buffer_8
  Register #(.width(4)) register_4 (.D(controlled_buffer_7_out), .Q(register_4_q), .clk(clock_1_out));  // open: en, clr
  assign controlled_buffer_9_out = in_5 ? register_4_q : 4'bz;  // Controlled_Buffer controlled_buffer_9
  Multiplexer #(.select(2), .width(4)) multiplexer_1 (
    .in0(controlled_buffer_9_out), .in1(_1), .in2(_2), .out(multiplexer_1_out), .sel(S2), .en(S1));  // open: in3
  assign controlled_buffer_10_out = in_14 ? ALU_c : 4'bz;  // Controlled_Buffer controlled_buffer_10
  main ALU (
    .B(multiplexer_1_out), .in_2(controlled_buffer_4_out), .Carry_in(CY_in), .Command(Cmd_0), .S(Cmd_1),
    .out_7(CY_out), .C(ALU_c));
  Register #(.width(4)) register_5 (
    .D(controlled_buffer_10_out), .en(in_16), .Q(register_5_q), .clk(clock_1_out));  // open: clr
endmodule
