// Logisim project circuit.circ as structural Verilog: 1 circuit, main circuit main
module main (
  input  [12:0] in_1,
  input  [15:0] in_2,
  input  [1:0] BIT_16_17_for_CS,
  input  RAM_ROM_SELECT_BIT,
  input  in_5,
  output [15:0] out_6,
  output [7:0] out_7,
  output [7:0] out_8
);

  wire clock_1_out, decoder_1_out0, decoder_1_out1, decoder_1_out2, decoder_1_out3, not_1_out;

  not not_1 (not_1_out, RAM_ROM_SELECT_BIT);
  Decoder #(.select(2)) decoder_1 (
    .out0(decoder_1_out0), .out1(decoder_1_out1), .out2(decoder_1_out2), .out3(decoder_1_out3),
    .sel(BIT_16_17_for_CS), .en(RAM_ROM_SELECT_BIT));
  Clock clock_1 (.out(clock_1_out));
  ROM #(.addrWidth(13), .dataWidth(16)) rom_1 (.addr(in_1), .data(out_6), .sel(not_1_out));
  RAM #(.addrWidth(16)) ram_1 (
    .addr(in_2), .data(out_7), .sel(decoder_1_out0), .clk(clock_1_out), .ld(in_5));  // open: clr
  RAM #(.addrWidth(16)) ram_2 (
    .addr(in_2), .data(out_7), .sel(decoder_1_out1), .clk(clock_1_out), .ld(in_5));  // open: clr
  RAM #(.addrWidth(16)) ram_3 (
    .addr(in_2), .data(out_7), .sel(decoder_1_out2), .clk(clock_1_out), .ld(in_5));  // open: clr
  RAM #(.addrWidth(16)) ram_4 (
    .addr(in_2), .data(out_7), .sel(decoder_1_out3), .clk(clock_1_out), .ld(in_5));  // open: clr
  RAM #(.addrWidth(16)) ram_5 (
    .addr(in_2), .data(out_8), .sel(decoder_1_out0), .clk(clock_1_out), .ld(in_5));  // open: clr
  RAM #(.addrWidth(16)) ram_6 (
    .addr(in_2), .data(out_8), .sel(decoder_1_out1), .clk(clock_1_out), .ld(in_5));  // open: clr
  RAM #(.addrWidth(16)) ram_7 (
    .addr(in_2), .data(out_8), .sel(decoder_1_out2), .clk(clock_1_out), .ld(in_5));  // open: clr
  RAM #(.addrWidth(16)) ram_8 (
    .addr(in_2), .data(out_8), .sel(decoder_1_out3), .clk(clock_1_out), .ld(in_5));  // open: clr

  // Notes on the sheet:
  //   1KBX16  ROM
  //   contents of rom_1 (hex, n*v repeats v):
  //   5
  //   64K x 8 RAM Chips
endmodule
